# Fritzing sketch gpio_input_led (saved by Fritzing 0.9.1b)
breadboards: 1

parts:
  BeagleBone1 = BeagleBone Black
  R1 = Resistor [tolerance=±5% resistance=10k package="0805 [SMD]"]
  S2 = Momentary Switch [package=tactile-pth]
  R2 = Resistor [tolerance=±5% resistance=10k package="0805 [SMD]"]
  Q2 = NPN-Transistor [part_number=BC547 package="TO92 [THT]"]
  R3 = Resistor [tolerance=±5% resistance=10k package="0805 [SMD]"]
  R4 = Resistor [tolerance=±5% resistance=10 package="0805 [SMD]"]
  LED2 = smd LED [color="Red (633nm)" package="0603 [SMD]"]

nets:
  N1: BeagleBone1.no_name_yet#7, S2.2, LED2.anode
  N2: BeagleBone1.no_name_yet#12, R3.Pin_0
  N3: BeagleBone1.no_name_yet#24, R1.Pin_0
  N4: BeagleBone1.no_name_yet#45, R2.Pin_1, Q2.E
  N5: R1.Pin_1, S2.3, R2.Pin_0
  N6: Q2.B, R3.Pin_1
  N7: Q2.C, R4.Pin_1
  N8: R4.Pin_0, LED2.cathode

custom parts:
  BeagleBone Black: BeagleBone Black rev. A5B
