# Fritzing sketch gpio_led (saved by Fritzing 0.9.1b)
breadboards: 1

parts:
  BeagleBone1 = BeagleBone Black
  Q1 = NPN-Transistor [part_number=BC547 package="TO92 [THT]"]
  R2 = Resistor [tolerance=±5% resistance=10 package="0805 [SMD]"]
  R1 = Resistor [tolerance=±5% resistance=10k package="0805 [SMD]"]
  LED1 = smd LED [color="Red (633nm)" package="0603 [SMD]"]

nets:
  N1: BeagleBone1.no_name_yet#7, LED1.anode
  N2: BeagleBone1.no_name_yet#12, R1.Pin_0
  N3: BeagleBone1.no_name_yet#45, Q1.E
  N4: Q1.B, R1.Pin_1
  N5: Q1.C, R2.Pin_1
  N6: R2.Pin_0, LED1.cathode

custom parts:
  BeagleBone Black: BeagleBone Black rev. A5B
